# Fritzing sketch DistanceAlerter-Arduino (saved by Fritzing 0.9.3b)
breadboards: 1

parts:
  hc-sr1 = hc-sr04
  Part1 = Arduino Uno (Rev3)
  LED1 = LED - 5mm [color="Red (633nm)" package="5 mm [THT]"]
  Part2 = KY-006 Passive Buzzer Module [package="Breakout board"]
  R1 = Resistor [tolerance=±5% resistance=220 package=THT]

nets:
  VCC: hc-sr1.VCC, Part1.5V
  N1: hc-sr1.Trig, Part1.D12/MISO
  N2: hc-sr1.Echo, Part1.D11_PWM/MOSI
  GND: hc-sr1.GND, Part1.GND, LED1.cathode, Part2.-
  N3: Part1.D3_PWM, R1.Pin_1
  N4: Part1.D4, Part2.S
  N5: LED1.anode, R1.Pin_0

custom parts:
  KY-006 Passive Buzzer Module: Passive Piezoelectric Buzzer Module Keyes KY-006, it can produce a range of sound tones depending on the input frequency.
